# Fritzing sketch GY-219 (saved by Fritzing 0.9.3b)
breadboards: 1

parts:
  Part1 = Arduino Pro Mini v13
  J2 = Generic female header - 4 pins [form="♀ (female)" package=THT]
  J3 = female pin header, 2 pins [form="♀ (female)"]  # not connected

nets:
  N1: Part1.A4, J2.SDA
  N2: Part1.A5, J2.SCL
  GND: Part1.GND, J2.GND
  VCC: Part1.VCC, J2.VCC

custom parts:
  Generic female header - 4 pins: Generic female header
